// Logisim project 32Bit_ALU.circ as structural Verilog: 1 circuit, main circuit main
module main (
  input  [31:0] in_1,
  input  [31:0] in_2,
  input  [3:0] in_3,
  input  [31:0] in_4,
  output [31:0] out_5,
  output zero_flag
);

  wire [31:0] adder_1_out, and_1_out, nand_1_out, nor_1_out, or_1_out, subtractor_1_out;

  assign and_1_out = in_2 & in_1;  // AND_Gate and_1, 32 bits wide
  assign or_1_out = in_2 | in_1;  // OR_Gate or_1, 32 bits wide
  assign nand_1_out = ~(in_2 & in_1);  // NAND_Gate nand_1, 32 bits wide
  assign nor_1_out = ~(in_2 | in_1);  // NOR_Gate nor_1, 32 bits wide
  Adder #(.width(32)) adder_1 (.a(in_2), .b(in_1), .out(adder_1_out));  // open: cin, cout
  Subtractor #(.width(32)) subtractor_1 (.a(in_2), .b(in_1), .out(subtractor_1_out));  // open: bin, bout
  Multiplexer #(.disabled("Z"), .enable("true"), .select(4), .width(32)) multiplexer_1 (
    .in0(and_1_out), .in1(or_1_out), .in2(nand_1_out), .in3(nor_1_out), .in4(adder_1_out),
    .in5(subtractor_1_out), .out(out_5), .sel(in_3));  // open: in6, in7, in8, in9, in10, in11, in12, in13, in14, in15, en
  Comparator #(.mode("unsigned"), .width(32)) comparator_1 (.a(out_5), .b(in_4), .eq(zero_flag));  // open: gt, lt

  // Notes on the sheet:
  //   A
  //   B
  //   AND
  //   OR
  //   NAND
  //   NOR
  //   ADD
  //   SUB
  //   Mux
  //   Sel_bit
  //   Result
  //   comparator
endmodule
